// Digital circuit block_function.dig as structural Verilog
module block_function (
  input  [31:0] k0,
  input  [31:0] k1,
  input  [31:0] k2,
  input  [31:0] k3,
  input  [31:0] k4,
  input  [31:0] k5,
  input  [31:0] k6,
  input  [31:0] k7,
  input  [31:0] bc,
  input  [31:0] n0,
  input  [31:0] n1,
  input  [31:0] n2,
  output [31:0] o0,
  output [31:0] o1,
  output [31:0] o2,
  output [31:0] o3,
  output [31:0] o4,
  output [31:0] o5,
  output [31:0] o6,
  output [31:0] o7,
  output [31:0] o8,
  output [31:0] o9,
  output [31:0] o10,
  output [31:0] o11,
  output [31:0] o12,
  output [31:0] o13,
  output [31:0] o14,
  output [31:0] o15
);

  wire [31:0] inner_block_function_1_o0, inner_block_function_1_o1, inner_block_function_1_o2,
       inner_block_function_1_o3, inner_block_function_1_o4, inner_block_function_1_o5,
       inner_block_function_1_o6, inner_block_function_1_o7, inner_block_function_1_o8,
       inner_block_function_1_o9, inner_block_function_1_o10, inner_block_function_1_o11,
       inner_block_function_1_o12, inner_block_function_1_o13, inner_block_function_1_o14,
       inner_block_function_1_o15, inner_block_function_2_o0, inner_block_function_2_o1,
       inner_block_function_2_o2, inner_block_function_2_o3, inner_block_function_2_o4,
       inner_block_function_2_o5, inner_block_function_2_o6, inner_block_function_2_o7,
       inner_block_function_2_o8, inner_block_function_2_o9, inner_block_function_2_o10,
       inner_block_function_2_o11, inner_block_function_2_o12, inner_block_function_2_o13,
       inner_block_function_2_o14, inner_block_function_2_o15, inner_block_function_3_o0,
       inner_block_function_3_o1, inner_block_function_3_o2, inner_block_function_3_o3,
       inner_block_function_3_o4, inner_block_function_3_o5, inner_block_function_3_o6,
       inner_block_function_3_o7, inner_block_function_3_o8, inner_block_function_3_o9,
       inner_block_function_3_o10, inner_block_function_3_o11, inner_block_function_3_o12,
       inner_block_function_3_o13, inner_block_function_3_o14, inner_block_function_3_o15,
       inner_block_function_4_o0, inner_block_function_4_o1, inner_block_function_4_o2,
       inner_block_function_4_o3, inner_block_function_4_o4, inner_block_function_4_o5,
       inner_block_function_4_o6, inner_block_function_4_o7, inner_block_function_4_o8,
       inner_block_function_4_o9, inner_block_function_4_o10, inner_block_function_4_o11,
       inner_block_function_4_o12, inner_block_function_4_o13, inner_block_function_4_o14,
       inner_block_function_4_o15, inner_block_function_5_o0, inner_block_function_5_o1,
       inner_block_function_5_o2, inner_block_function_5_o3, inner_block_function_5_o4,
       inner_block_function_5_o5, inner_block_function_5_o6, inner_block_function_5_o7,
       inner_block_function_5_o8, inner_block_function_5_o9, inner_block_function_5_o10,
       inner_block_function_5_o11, inner_block_function_5_o12, inner_block_function_5_o13,
       inner_block_function_5_o14, inner_block_function_5_o15, inner_block_function_6_o0,
       inner_block_function_6_o1, inner_block_function_6_o2, inner_block_function_6_o3,
       inner_block_function_6_o4, inner_block_function_6_o5, inner_block_function_6_o6,
       inner_block_function_6_o7, inner_block_function_6_o8, inner_block_function_6_o9,
       inner_block_function_6_o10, inner_block_function_6_o11, inner_block_function_6_o12,
       inner_block_function_6_o13, inner_block_function_6_o14, inner_block_function_6_o15,
       inner_block_function_7_o0, inner_block_function_7_o1, inner_block_function_7_o2,
       inner_block_function_7_o3, inner_block_function_7_o4, inner_block_function_7_o5,
       inner_block_function_7_o6, inner_block_function_7_o7, inner_block_function_7_o8,
       inner_block_function_7_o9, inner_block_function_7_o10, inner_block_function_7_o11,
       inner_block_function_7_o12, inner_block_function_7_o13, inner_block_function_7_o14,
       inner_block_function_7_o15, inner_block_function_8_o0, inner_block_function_8_o1,
       inner_block_function_8_o2, inner_block_function_8_o3, inner_block_function_8_o4,
       inner_block_function_8_o5, inner_block_function_8_o6, inner_block_function_8_o7,
       inner_block_function_8_o8, inner_block_function_8_o9, inner_block_function_8_o10,
       inner_block_function_8_o11, inner_block_function_8_o12, inner_block_function_8_o13,
       inner_block_function_8_o14, inner_block_function_8_o15, inner_block_function_9_o0,
       inner_block_function_9_o1, inner_block_function_9_o2, inner_block_function_9_o3,
       inner_block_function_9_o4, inner_block_function_9_o5, inner_block_function_9_o6,
       inner_block_function_9_o7, inner_block_function_9_o8, inner_block_function_9_o9,
       inner_block_function_9_o10, inner_block_function_9_o11, inner_block_function_9_o12,
       inner_block_function_9_o13, inner_block_function_9_o14, inner_block_function_9_o15,
       inner_block_function_10_o0, inner_block_function_10_o1, inner_block_function_10_o2,
       inner_block_function_10_o3, inner_block_function_10_o4, inner_block_function_10_o5,
       inner_block_function_10_o6, inner_block_function_10_o7, inner_block_function_10_o8,
       inner_block_function_10_o9, inner_block_function_10_o10, inner_block_function_10_o11,
       inner_block_function_10_o12, inner_block_function_10_o13, inner_block_function_10_o14,
       inner_block_function_10_o15;

  inner_block_function inner_block_function_1 (
    .i0(32'h61707865), .i1(32'h3320646e), .i2(32'h79622d32), .i3(32'h6b206574), .i4(k0), .i5(k1), .i6(k2),
    .i7(k3), .i8(k4), .i9(k5), .i10(k6), .i11(k7), .i12(bc), .i13(n0), .i14(n1), .i15(n2),
    .o0(inner_block_function_1_o0), .o1(inner_block_function_1_o1), .o2(inner_block_function_1_o2),
    .o3(inner_block_function_1_o3), .o4(inner_block_function_1_o4), .o5(inner_block_function_1_o5),
    .o6(inner_block_function_1_o6), .o7(inner_block_function_1_o7), .o8(inner_block_function_1_o8),
    .o9(inner_block_function_1_o9), .o10(inner_block_function_1_o10), .o11(inner_block_function_1_o11),
    .o12(inner_block_function_1_o12), .o13(inner_block_function_1_o13), .o14(inner_block_function_1_o14),
    .o15(inner_block_function_1_o15));
  inner_block_function inner_block_function_2 (
    .i0(inner_block_function_1_o0), .i1(inner_block_function_1_o1), .i2(inner_block_function_1_o2),
    .i3(inner_block_function_1_o3), .i4(inner_block_function_1_o4), .i5(inner_block_function_1_o5),
    .i6(inner_block_function_1_o6), .i7(inner_block_function_1_o7), .i8(inner_block_function_1_o8),
    .i9(inner_block_function_1_o9), .i10(inner_block_function_1_o10), .i11(inner_block_function_1_o11),
    .i12(inner_block_function_1_o12), .i13(inner_block_function_1_o13), .i14(inner_block_function_1_o14),
    .i15(inner_block_function_1_o15), .o0(inner_block_function_2_o0), .o1(inner_block_function_2_o1),
    .o2(inner_block_function_2_o2), .o3(inner_block_function_2_o3), .o4(inner_block_function_2_o4),
    .o5(inner_block_function_2_o5), .o6(inner_block_function_2_o6), .o7(inner_block_function_2_o7),
    .o8(inner_block_function_2_o8), .o9(inner_block_function_2_o9), .o10(inner_block_function_2_o10),
    .o11(inner_block_function_2_o11), .o12(inner_block_function_2_o12), .o13(inner_block_function_2_o13),
    .o14(inner_block_function_2_o14), .o15(inner_block_function_2_o15));
  inner_block_function inner_block_function_3 (
    .i0(inner_block_function_2_o0), .i1(inner_block_function_2_o1), .i2(inner_block_function_2_o2),
    .i3(inner_block_function_2_o3), .i4(inner_block_function_2_o4), .i5(inner_block_function_2_o5),
    .i6(inner_block_function_2_o6), .i7(inner_block_function_2_o7), .i8(inner_block_function_2_o8),
    .i9(inner_block_function_2_o9), .i10(inner_block_function_2_o10), .i11(inner_block_function_2_o11),
    .i12(inner_block_function_2_o12), .i13(inner_block_function_2_o13), .i14(inner_block_function_2_o14),
    .i15(inner_block_function_2_o15), .o0(inner_block_function_3_o0), .o1(inner_block_function_3_o1),
    .o2(inner_block_function_3_o2), .o3(inner_block_function_3_o3), .o4(inner_block_function_3_o4),
    .o5(inner_block_function_3_o5), .o6(inner_block_function_3_o6), .o7(inner_block_function_3_o7),
    .o8(inner_block_function_3_o8), .o9(inner_block_function_3_o9), .o10(inner_block_function_3_o10),
    .o11(inner_block_function_3_o11), .o12(inner_block_function_3_o12), .o13(inner_block_function_3_o13),
    .o14(inner_block_function_3_o14), .o15(inner_block_function_3_o15));
  inner_block_function inner_block_function_4 (
    .i0(inner_block_function_3_o0), .i1(inner_block_function_3_o1), .i2(inner_block_function_3_o2),
    .i3(inner_block_function_3_o3), .i4(inner_block_function_3_o4), .i5(inner_block_function_3_o5),
    .i6(inner_block_function_3_o6), .i7(inner_block_function_3_o7), .i8(inner_block_function_3_o8),
    .i9(inner_block_function_3_o9), .i10(inner_block_function_3_o10), .i11(inner_block_function_3_o11),
    .i12(inner_block_function_3_o12), .i13(inner_block_function_3_o13), .i14(inner_block_function_3_o14),
    .i15(inner_block_function_3_o15), .o0(inner_block_function_4_o0), .o1(inner_block_function_4_o1),
    .o2(inner_block_function_4_o2), .o3(inner_block_function_4_o3), .o4(inner_block_function_4_o4),
    .o5(inner_block_function_4_o5), .o6(inner_block_function_4_o6), .o7(inner_block_function_4_o7),
    .o8(inner_block_function_4_o8), .o9(inner_block_function_4_o9), .o10(inner_block_function_4_o10),
    .o11(inner_block_function_4_o11), .o12(inner_block_function_4_o12), .o13(inner_block_function_4_o13),
    .o14(inner_block_function_4_o14), .o15(inner_block_function_4_o15));
  inner_block_function inner_block_function_5 (
    .i0(inner_block_function_4_o0), .i1(inner_block_function_4_o1), .i2(inner_block_function_4_o2),
    .i3(inner_block_function_4_o3), .i4(inner_block_function_4_o4), .i5(inner_block_function_4_o5),
    .i6(inner_block_function_4_o6), .i7(inner_block_function_4_o7), .i8(inner_block_function_4_o8),
    .i9(inner_block_function_4_o9), .i10(inner_block_function_4_o10), .i11(inner_block_function_4_o11),
    .i12(inner_block_function_4_o12), .i13(inner_block_function_4_o13), .i14(inner_block_function_4_o14),
    .i15(inner_block_function_4_o15), .o0(inner_block_function_5_o0), .o1(inner_block_function_5_o1),
    .o2(inner_block_function_5_o2), .o3(inner_block_function_5_o3), .o4(inner_block_function_5_o4),
    .o5(inner_block_function_5_o5), .o6(inner_block_function_5_o6), .o7(inner_block_function_5_o7),
    .o8(inner_block_function_5_o8), .o9(inner_block_function_5_o9), .o10(inner_block_function_5_o10),
    .o11(inner_block_function_5_o11), .o12(inner_block_function_5_o12), .o13(inner_block_function_5_o13),
    .o14(inner_block_function_5_o14), .o15(inner_block_function_5_o15));
  inner_block_function inner_block_function_6 (
    .i0(inner_block_function_5_o0), .i1(inner_block_function_5_o1), .i2(inner_block_function_5_o2),
    .i3(inner_block_function_5_o3), .i4(inner_block_function_5_o4), .i5(inner_block_function_5_o5),
    .i6(inner_block_function_5_o6), .i7(inner_block_function_5_o7), .i8(inner_block_function_5_o8),
    .i9(inner_block_function_5_o9), .i10(inner_block_function_5_o10), .i11(inner_block_function_5_o11),
    .i12(inner_block_function_5_o12), .i13(inner_block_function_5_o13), .i14(inner_block_function_5_o14),
    .i15(inner_block_function_5_o15), .o0(inner_block_function_6_o0), .o1(inner_block_function_6_o1),
    .o2(inner_block_function_6_o2), .o3(inner_block_function_6_o3), .o4(inner_block_function_6_o4),
    .o5(inner_block_function_6_o5), .o6(inner_block_function_6_o6), .o7(inner_block_function_6_o7),
    .o8(inner_block_function_6_o8), .o9(inner_block_function_6_o9), .o10(inner_block_function_6_o10),
    .o11(inner_block_function_6_o11), .o12(inner_block_function_6_o12), .o13(inner_block_function_6_o13),
    .o14(inner_block_function_6_o14), .o15(inner_block_function_6_o15));
  inner_block_function inner_block_function_7 (
    .i0(inner_block_function_6_o0), .i1(inner_block_function_6_o1), .i2(inner_block_function_6_o2),
    .i3(inner_block_function_6_o3), .i4(inner_block_function_6_o4), .i5(inner_block_function_6_o5),
    .i6(inner_block_function_6_o6), .i7(inner_block_function_6_o7), .i8(inner_block_function_6_o8),
    .i9(inner_block_function_6_o9), .i10(inner_block_function_6_o10), .i11(inner_block_function_6_o11),
    .i12(inner_block_function_6_o12), .i13(inner_block_function_6_o13), .i14(inner_block_function_6_o14),
    .i15(inner_block_function_6_o15), .o0(inner_block_function_7_o0), .o1(inner_block_function_7_o1),
    .o2(inner_block_function_7_o2), .o3(inner_block_function_7_o3), .o4(inner_block_function_7_o4),
    .o5(inner_block_function_7_o5), .o6(inner_block_function_7_o6), .o7(inner_block_function_7_o7),
    .o8(inner_block_function_7_o8), .o9(inner_block_function_7_o9), .o10(inner_block_function_7_o10),
    .o11(inner_block_function_7_o11), .o12(inner_block_function_7_o12), .o13(inner_block_function_7_o13),
    .o14(inner_block_function_7_o14), .o15(inner_block_function_7_o15));
  inner_block_function inner_block_function_8 (
    .i0(inner_block_function_7_o0), .i1(inner_block_function_7_o1), .i2(inner_block_function_7_o2),
    .i3(inner_block_function_7_o3), .i4(inner_block_function_7_o4), .i5(inner_block_function_7_o5),
    .i6(inner_block_function_7_o6), .i7(inner_block_function_7_o7), .i8(inner_block_function_7_o8),
    .i9(inner_block_function_7_o9), .i10(inner_block_function_7_o10), .i11(inner_block_function_7_o11),
    .i12(inner_block_function_7_o12), .i13(inner_block_function_7_o13), .i14(inner_block_function_7_o14),
    .i15(inner_block_function_7_o15), .o0(inner_block_function_8_o0), .o1(inner_block_function_8_o1),
    .o2(inner_block_function_8_o2), .o3(inner_block_function_8_o3), .o4(inner_block_function_8_o4),
    .o5(inner_block_function_8_o5), .o6(inner_block_function_8_o6), .o7(inner_block_function_8_o7),
    .o8(inner_block_function_8_o8), .o9(inner_block_function_8_o9), .o10(inner_block_function_8_o10),
    .o11(inner_block_function_8_o11), .o12(inner_block_function_8_o12), .o13(inner_block_function_8_o13),
    .o14(inner_block_function_8_o14), .o15(inner_block_function_8_o15));
  inner_block_function inner_block_function_9 (
    .i0(inner_block_function_8_o0), .i1(inner_block_function_8_o1), .i2(inner_block_function_8_o2),
    .i3(inner_block_function_8_o3), .i4(inner_block_function_8_o4), .i5(inner_block_function_8_o5),
    .i6(inner_block_function_8_o6), .i7(inner_block_function_8_o7), .i8(inner_block_function_8_o8),
    .i9(inner_block_function_8_o9), .i10(inner_block_function_8_o10), .i11(inner_block_function_8_o11),
    .i12(inner_block_function_8_o12), .i13(inner_block_function_8_o13), .i14(inner_block_function_8_o14),
    .i15(inner_block_function_8_o15), .o0(inner_block_function_9_o0), .o1(inner_block_function_9_o1),
    .o2(inner_block_function_9_o2), .o3(inner_block_function_9_o3), .o4(inner_block_function_9_o4),
    .o5(inner_block_function_9_o5), .o6(inner_block_function_9_o6), .o7(inner_block_function_9_o7),
    .o8(inner_block_function_9_o8), .o9(inner_block_function_9_o9), .o10(inner_block_function_9_o10),
    .o11(inner_block_function_9_o11), .o12(inner_block_function_9_o12), .o13(inner_block_function_9_o13),
    .o14(inner_block_function_9_o14), .o15(inner_block_function_9_o15));
  inner_block_function inner_block_function_10 (
    .i0(inner_block_function_9_o0), .i1(inner_block_function_9_o1), .i2(inner_block_function_9_o2),
    .i3(inner_block_function_9_o3), .i4(inner_block_function_9_o4), .i5(inner_block_function_9_o5),
    .i6(inner_block_function_9_o6), .i7(inner_block_function_9_o7), .i8(inner_block_function_9_o8),
    .i9(inner_block_function_9_o9), .i10(inner_block_function_9_o10), .i11(inner_block_function_9_o11),
    .i12(inner_block_function_9_o12), .i13(inner_block_function_9_o13), .i14(inner_block_function_9_o14),
    .i15(inner_block_function_9_o15), .o0(inner_block_function_10_o0), .o1(inner_block_function_10_o1),
    .o2(inner_block_function_10_o2), .o3(inner_block_function_10_o3), .o4(inner_block_function_10_o4),
    .o5(inner_block_function_10_o5), .o6(inner_block_function_10_o6), .o7(inner_block_function_10_o7),
    .o8(inner_block_function_10_o8), .o9(inner_block_function_10_o9), .o10(inner_block_function_10_o10),
    .o11(inner_block_function_10_o11), .o12(inner_block_function_10_o12), .o13(inner_block_function_10_o13),
    .o14(inner_block_function_10_o14), .o15(inner_block_function_10_o15));
  Add #(.Bits(32)) add_1 (.a(32'h61707865), .b(inner_block_function_10_o0), .c_i(1'b0), .s(o0));  // open: c_o
  Add #(.Bits(32)) add_2 (.a(32'h3320646e), .b(inner_block_function_10_o1), .c_i(1'b0), .s(o1));  // open: c_o
  Add #(.Bits(32)) add_3 (.a(32'h79622d32), .b(inner_block_function_10_o2), .c_i(1'b0), .s(o2));  // open: c_o
  Add #(.Bits(32)) add_4 (.a(32'h6b206574), .b(inner_block_function_10_o3), .c_i(1'b0), .s(o3));  // open: c_o
  Add #(.Bits(32)) add_5 (.a(k0), .b(inner_block_function_10_o4), .c_i(1'b0), .s(o4));  // open: c_o
  Add #(.Bits(32)) add_6 (.a(k1), .b(inner_block_function_10_o5), .c_i(1'b0), .s(o5));  // open: c_o
  Add #(.Bits(32)) add_7 (.a(k2), .b(inner_block_function_10_o6), .c_i(1'b0), .s(o6));  // open: c_o
  Add #(.Bits(32)) add_8 (.a(k3), .b(inner_block_function_10_o7), .c_i(1'b0), .s(o7));  // open: c_o
  Add #(.Bits(32)) add_9 (.a(k4), .b(inner_block_function_10_o8), .c_i(1'b0), .s(o8));  // open: c_o
  Add #(.Bits(32)) add_10 (.a(k5), .b(inner_block_function_10_o9), .c_i(1'b0), .s(o9));  // open: c_o
  Add #(.Bits(32)) add_11 (.a(k6), .b(inner_block_function_10_o10), .c_i(1'b0), .s(o10));  // open: c_o
  Add #(.Bits(32)) add_12 (.a(k7), .b(inner_block_function_10_o11), .c_i(1'b0), .s(o11));  // open: c_o
  Add #(.Bits(32)) add_13 (.a(bc), .b(inner_block_function_10_o12), .c_i(1'b0), .s(o12));  // open: c_o
  Add #(.Bits(32)) add_14 (.a(n0), .b(inner_block_function_10_o13), .c_i(1'b0), .s(o13));  // open: c_o
  Add #(.Bits(32)) add_15 (.a(n1), .b(inner_block_function_10_o14), .c_i(1'b0), .s(o14));  // open: c_o
  Add #(.Bits(32)) add_16 (.a(n2), .b(inner_block_function_10_o15), .c_i(1'b0), .s(o15));  // open: c_o
endmodule

/* Test case test0:
k0 k1 k2 k3 k4 k5 k6 k7 bc n0 n1 n2 o0 o1 o2 o3 o4 o5 o6 o7 o8 o9 o10 o11 o12 o13 o14 o15

# RFC 8439 2.3.2 - ChaCha20 block, final output (after adding original state)
0x03020100 0x07060504 0x0b0a0908 0x0f0e0d0c 0x13121110 0x17161514 0x1b1a1918 0x1f1e1d1c 0x00000001 0x09000000 0x4a000000 0x00000000 0xe4e7f110 0x15593bd1 0x1fdd0f50 0xc47120a3 0xc7f4d1c7 0x0368c033 0x9aaa2204 0x4e6cd4c3 0x466482d2 0x09aa9f07 0x05d7c214 0xa2028bd9 0xd19c12b5 0xb94e16de 0xe883d0cb 0x4e3c50a2
*/
