// Digital circuit inner_block_function.dig as structural Verilog
module inner_block_function (
  input  [31:0] i0,
  input  [31:0] i1,
  input  [31:0] i2,
  input  [31:0] i3,
  input  [31:0] i4,
  input  [31:0] i5,
  input  [31:0] i6,
  input  [31:0] i7,
  input  [31:0] i8,
  input  [31:0] i9,
  input  [31:0] i10,
  input  [31:0] i11,
  input  [31:0] i12,
  input  [31:0] i13,
  input  [31:0] i14,
  input  [31:0] i15,
  output [31:0] o0,
  output [31:0] o1,
  output [31:0] o2,
  output [31:0] o3,
  output [31:0] o4,
  output [31:0] o5,
  output [31:0] o6,
  output [31:0] o7,
  output [31:0] o8,
  output [31:0] o9,
  output [31:0] o10,
  output [31:0] o11,
  output [31:0] o12,
  output [31:0] o13,
  output [31:0] o14,
  output [31:0] o15
);

  wire [31:0] state_quarter_round_1_o0, state_quarter_round_1_o1, state_quarter_round_1_o2,
       state_quarter_round_1_o3, state_quarter_round_1_o4, state_quarter_round_1_o5,
       state_quarter_round_1_o6, state_quarter_round_1_o7, state_quarter_round_1_o8,
       state_quarter_round_1_o9, state_quarter_round_1_o10, state_quarter_round_1_o11,
       state_quarter_round_1_o12, state_quarter_round_1_o13, state_quarter_round_1_o14,
       state_quarter_round_1_o15, state_quarter_round_2_o0, state_quarter_round_2_o1,
       state_quarter_round_2_o2, state_quarter_round_2_o3, state_quarter_round_2_o4,
       state_quarter_round_2_o5, state_quarter_round_2_o6, state_quarter_round_2_o7,
       state_quarter_round_2_o8, state_quarter_round_2_o9, state_quarter_round_2_o10,
       state_quarter_round_2_o11, state_quarter_round_2_o12, state_quarter_round_2_o13,
       state_quarter_round_2_o14, state_quarter_round_2_o15, state_quarter_round_3_o0,
       state_quarter_round_3_o1, state_quarter_round_3_o2, state_quarter_round_3_o3,
       state_quarter_round_3_o4, state_quarter_round_3_o5, state_quarter_round_3_o6,
       state_quarter_round_3_o7, state_quarter_round_3_o8, state_quarter_round_3_o9,
       state_quarter_round_3_o10, state_quarter_round_3_o11, state_quarter_round_3_o12,
       state_quarter_round_3_o13, state_quarter_round_3_o14, state_quarter_round_3_o15,
       state_quarter_round_4_o0, state_quarter_round_4_o1, state_quarter_round_4_o2,
       state_quarter_round_4_o3, state_quarter_round_4_o4, state_quarter_round_4_o5,
       state_quarter_round_4_o6, state_quarter_round_4_o7, state_quarter_round_4_o8,
       state_quarter_round_4_o9, state_quarter_round_4_o10, state_quarter_round_4_o11,
       state_quarter_round_4_o12, state_quarter_round_4_o13, state_quarter_round_4_o14,
       state_quarter_round_4_o15, state_quarter_round_5_o0, state_quarter_round_5_o1,
       state_quarter_round_5_o2, state_quarter_round_5_o3, state_quarter_round_5_o4,
       state_quarter_round_5_o5, state_quarter_round_5_o6, state_quarter_round_5_o7,
       state_quarter_round_5_o8, state_quarter_round_5_o9, state_quarter_round_5_o10,
       state_quarter_round_5_o11, state_quarter_round_5_o12, state_quarter_round_5_o13,
       state_quarter_round_5_o14, state_quarter_round_5_o15, state_quarter_round_6_o0,
       state_quarter_round_6_o1, state_quarter_round_6_o2, state_quarter_round_6_o3,
       state_quarter_round_6_o4, state_quarter_round_6_o5, state_quarter_round_6_o6,
       state_quarter_round_6_o7, state_quarter_round_6_o8, state_quarter_round_6_o9,
       state_quarter_round_6_o10, state_quarter_round_6_o11, state_quarter_round_6_o12,
       state_quarter_round_6_o13, state_quarter_round_6_o14, state_quarter_round_6_o15,
       state_quarter_round_7_o0, state_quarter_round_7_o1, state_quarter_round_7_o2,
       state_quarter_round_7_o3, state_quarter_round_7_o4, state_quarter_round_7_o5,
       state_quarter_round_7_o6, state_quarter_round_7_o7, state_quarter_round_7_o8,
       state_quarter_round_7_o9, state_quarter_round_7_o10, state_quarter_round_7_o11,
       state_quarter_round_7_o12, state_quarter_round_7_o13, state_quarter_round_7_o14,
       state_quarter_round_7_o15;

  state_quarter_round state_quarter_round_1 (
    .i0(i0), .i1(i1), .i2(i2), .i3(i3), .i4(i4), .i5(i5), .i6(i6), .i7(i7), .i8(i8), .i9(i9), .i10(i10),
    .i11(i11), .i12(i12), .i13(i13), .i14(i14), .i15(i15), .x(4'b0000), .y(4'b0100), .z(4'b1000),
    .w(4'b1100), .o0(state_quarter_round_1_o0), .o1(state_quarter_round_1_o1), .o2(state_quarter_round_1_o2),
    .o3(state_quarter_round_1_o3), .o4(state_quarter_round_1_o4), .o5(state_quarter_round_1_o5),
    .o6(state_quarter_round_1_o6), .o7(state_quarter_round_1_o7), .o8(state_quarter_round_1_o8),
    .o9(state_quarter_round_1_o9), .o10(state_quarter_round_1_o10), .o11(state_quarter_round_1_o11),
    .o12(state_quarter_round_1_o12), .o13(state_quarter_round_1_o13), .o14(state_quarter_round_1_o14),
    .o15(state_quarter_round_1_o15));
  state_quarter_round state_quarter_round_2 (
    .i0(state_quarter_round_1_o0), .i1(state_quarter_round_1_o1), .i2(state_quarter_round_1_o2),
    .i3(state_quarter_round_1_o3), .i4(state_quarter_round_1_o4), .i5(state_quarter_round_1_o5),
    .i6(state_quarter_round_1_o6), .i7(state_quarter_round_1_o7), .i8(state_quarter_round_1_o8),
    .i9(state_quarter_round_1_o9), .i10(state_quarter_round_1_o10), .i11(state_quarter_round_1_o11),
    .i12(state_quarter_round_1_o12), .i13(state_quarter_round_1_o13), .i14(state_quarter_round_1_o14),
    .i15(state_quarter_round_1_o15), .x(4'b0001), .y(4'b0101), .z(4'b1001), .w(4'b1101),
    .o0(state_quarter_round_2_o0), .o1(state_quarter_round_2_o1), .o2(state_quarter_round_2_o2),
    .o3(state_quarter_round_2_o3), .o4(state_quarter_round_2_o4), .o5(state_quarter_round_2_o5),
    .o6(state_quarter_round_2_o6), .o7(state_quarter_round_2_o7), .o8(state_quarter_round_2_o8),
    .o9(state_quarter_round_2_o9), .o10(state_quarter_round_2_o10), .o11(state_quarter_round_2_o11),
    .o12(state_quarter_round_2_o12), .o13(state_quarter_round_2_o13), .o14(state_quarter_round_2_o14),
    .o15(state_quarter_round_2_o15));
  state_quarter_round state_quarter_round_3 (
    .i0(state_quarter_round_2_o0), .i1(state_quarter_round_2_o1), .i2(state_quarter_round_2_o2),
    .i3(state_quarter_round_2_o3), .i4(state_quarter_round_2_o4), .i5(state_quarter_round_2_o5),
    .i6(state_quarter_round_2_o6), .i7(state_quarter_round_2_o7), .i8(state_quarter_round_2_o8),
    .i9(state_quarter_round_2_o9), .i10(state_quarter_round_2_o10), .i11(state_quarter_round_2_o11),
    .i12(state_quarter_round_2_o12), .i13(state_quarter_round_2_o13), .i14(state_quarter_round_2_o14),
    .i15(state_quarter_round_2_o15), .x(4'b0010), .y(4'b0110), .z(4'b1010), .w(4'b1110),
    .o0(state_quarter_round_3_o0), .o1(state_quarter_round_3_o1), .o2(state_quarter_round_3_o2),
    .o3(state_quarter_round_3_o3), .o4(state_quarter_round_3_o4), .o5(state_quarter_round_3_o5),
    .o6(state_quarter_round_3_o6), .o7(state_quarter_round_3_o7), .o8(state_quarter_round_3_o8),
    .o9(state_quarter_round_3_o9), .o10(state_quarter_round_3_o10), .o11(state_quarter_round_3_o11),
    .o12(state_quarter_round_3_o12), .o13(state_quarter_round_3_o13), .o14(state_quarter_round_3_o14),
    .o15(state_quarter_round_3_o15));
  state_quarter_round state_quarter_round_4 (
    .i0(state_quarter_round_3_o0), .i1(state_quarter_round_3_o1), .i2(state_quarter_round_3_o2),
    .i3(state_quarter_round_3_o3), .i4(state_quarter_round_3_o4), .i5(state_quarter_round_3_o5),
    .i6(state_quarter_round_3_o6), .i7(state_quarter_round_3_o7), .i8(state_quarter_round_3_o8),
    .i9(state_quarter_round_3_o9), .i10(state_quarter_round_3_o10), .i11(state_quarter_round_3_o11),
    .i12(state_quarter_round_3_o12), .i13(state_quarter_round_3_o13), .i14(state_quarter_round_3_o14),
    .i15(state_quarter_round_3_o15), .x(4'b0011), .y(4'b0111), .z(4'b1011), .w(4'b1111),
    .o0(state_quarter_round_4_o0), .o1(state_quarter_round_4_o1), .o2(state_quarter_round_4_o2),
    .o3(state_quarter_round_4_o3), .o4(state_quarter_round_4_o4), .o5(state_quarter_round_4_o5),
    .o6(state_quarter_round_4_o6), .o7(state_quarter_round_4_o7), .o8(state_quarter_round_4_o8),
    .o9(state_quarter_round_4_o9), .o10(state_quarter_round_4_o10), .o11(state_quarter_round_4_o11),
    .o12(state_quarter_round_4_o12), .o13(state_quarter_round_4_o13), .o14(state_quarter_round_4_o14),
    .o15(state_quarter_round_4_o15));
  state_quarter_round state_quarter_round_5 (
    .i0(state_quarter_round_4_o0), .i1(state_quarter_round_4_o1), .i2(state_quarter_round_4_o2),
    .i3(state_quarter_round_4_o3), .i4(state_quarter_round_4_o4), .i5(state_quarter_round_4_o5),
    .i6(state_quarter_round_4_o6), .i7(state_quarter_round_4_o7), .i8(state_quarter_round_4_o8),
    .i9(state_quarter_round_4_o9), .i10(state_quarter_round_4_o10), .i11(state_quarter_round_4_o11),
    .i12(state_quarter_round_4_o12), .i13(state_quarter_round_4_o13), .i14(state_quarter_round_4_o14),
    .i15(state_quarter_round_4_o15), .x(4'b0000), .y(4'b0101), .z(4'b1010), .w(4'b1111),
    .o0(state_quarter_round_5_o0), .o1(state_quarter_round_5_o1), .o2(state_quarter_round_5_o2),
    .o3(state_quarter_round_5_o3), .o4(state_quarter_round_5_o4), .o5(state_quarter_round_5_o5),
    .o6(state_quarter_round_5_o6), .o7(state_quarter_round_5_o7), .o8(state_quarter_round_5_o8),
    .o9(state_quarter_round_5_o9), .o10(state_quarter_round_5_o10), .o11(state_quarter_round_5_o11),
    .o12(state_quarter_round_5_o12), .o13(state_quarter_round_5_o13), .o14(state_quarter_round_5_o14),
    .o15(state_quarter_round_5_o15));
  state_quarter_round state_quarter_round_6 (
    .i0(state_quarter_round_5_o0), .i1(state_quarter_round_5_o1), .i2(state_quarter_round_5_o2),
    .i3(state_quarter_round_5_o3), .i4(state_quarter_round_5_o4), .i5(state_quarter_round_5_o5),
    .i6(state_quarter_round_5_o6), .i7(state_quarter_round_5_o7), .i8(state_quarter_round_5_o8),
    .i9(state_quarter_round_5_o9), .i10(state_quarter_round_5_o10), .i11(state_quarter_round_5_o11),
    .i12(state_quarter_round_5_o12), .i13(state_quarter_round_5_o13), .i14(state_quarter_round_5_o14),
    .i15(state_quarter_round_5_o15), .x(4'b0001), .y(4'b0110), .z(4'b1011), .w(4'b1100),
    .o0(state_quarter_round_6_o0), .o1(state_quarter_round_6_o1), .o2(state_quarter_round_6_o2),
    .o3(state_quarter_round_6_o3), .o4(state_quarter_round_6_o4), .o5(state_quarter_round_6_o5),
    .o6(state_quarter_round_6_o6), .o7(state_quarter_round_6_o7), .o8(state_quarter_round_6_o8),
    .o9(state_quarter_round_6_o9), .o10(state_quarter_round_6_o10), .o11(state_quarter_round_6_o11),
    .o12(state_quarter_round_6_o12), .o13(state_quarter_round_6_o13), .o14(state_quarter_round_6_o14),
    .o15(state_quarter_round_6_o15));
  state_quarter_round state_quarter_round_7 (
    .i0(state_quarter_round_6_o0), .i1(state_quarter_round_6_o1), .i2(state_quarter_round_6_o2),
    .i3(state_quarter_round_6_o3), .i4(state_quarter_round_6_o4), .i5(state_quarter_round_6_o5),
    .i6(state_quarter_round_6_o6), .i7(state_quarter_round_6_o7), .i8(state_quarter_round_6_o8),
    .i9(state_quarter_round_6_o9), .i10(state_quarter_round_6_o10), .i11(state_quarter_round_6_o11),
    .i12(state_quarter_round_6_o12), .i13(state_quarter_round_6_o13), .i14(state_quarter_round_6_o14),
    .i15(state_quarter_round_6_o15), .x(4'b0010), .y(4'b0111), .z(4'b1000), .w(4'b1101),
    .o0(state_quarter_round_7_o0), .o1(state_quarter_round_7_o1), .o2(state_quarter_round_7_o2),
    .o3(state_quarter_round_7_o3), .o4(state_quarter_round_7_o4), .o5(state_quarter_round_7_o5),
    .o6(state_quarter_round_7_o6), .o7(state_quarter_round_7_o7), .o8(state_quarter_round_7_o8),
    .o9(state_quarter_round_7_o9), .o10(state_quarter_round_7_o10), .o11(state_quarter_round_7_o11),
    .o12(state_quarter_round_7_o12), .o13(state_quarter_round_7_o13), .o14(state_quarter_round_7_o14),
    .o15(state_quarter_round_7_o15));
  state_quarter_round state_quarter_round_8 (
    .i0(state_quarter_round_7_o0), .i1(state_quarter_round_7_o1), .i2(state_quarter_round_7_o2),
    .i3(state_quarter_round_7_o3), .i4(state_quarter_round_7_o4), .i5(state_quarter_round_7_o5),
    .i6(state_quarter_round_7_o6), .i7(state_quarter_round_7_o7), .i8(state_quarter_round_7_o8),
    .i9(state_quarter_round_7_o9), .i10(state_quarter_round_7_o10), .i11(state_quarter_round_7_o11),
    .i12(state_quarter_round_7_o12), .i13(state_quarter_round_7_o13), .i14(state_quarter_round_7_o14),
    .i15(state_quarter_round_7_o15), .x(4'b0011), .y(4'b0100), .z(4'b1001), .w(4'b1110), .o0(o0), .o1(o1),
    .o2(o2), .o3(o3), .o4(o4), .o5(o5), .o6(o6), .o7(o7), .o8(o8), .o9(o9), .o10(o10), .o11(o11), .o12(o12),
    .o13(o13), .o14(o14), .o15(o15));
endmodule

/* Test case test0:
i0 i1 i2 i3 i4 i5 i6 i7 i8 i9 i10 i11 i12 i13 i14 i15 o0 o1 o2 o3 o4 o5 o6 o7 o8 o9 o10 o11 o12 o13 o14 o15
0x61707865 0x3320646e 0x79622d32 0x6b206574 0x03020100 0x07060504 0x0b0a0908 0x0f0e0d0c 0x13121110 0x17161514 0x1b1a1918 0x1f1e1d1c 0x00000001 0x09000000 0x4a000000 0x00000000 0xcd52e917 0x85ab03b4 0xb3457395 0xf96de7dd 0xc4b7cd22 0x5c2e187a 0xc95eb461 0x316c801a 0x7bf7d740 0x7eddd644 0xf1a1bdf5 0x761246ca 0x6b0d58a3 0x6798471a 0xd737f167 0xf173888d
0xcd52e917 0x85ab03b4 0xb3457395 0xf96de7dd 0xc4b7cd22 0x5c2e187a 0xc95eb461 0x316c801a 0x7bf7d740 0x7eddd644 0xf1a1bdf5 0x761246ca 0x6b0d58a3 0x6798471a 0xd737f167 0xf173888d 0xcf1a7584 0x048927ec 0x54051fda 0xc244ff28 0x901d2f40 0x7974b81c 0x378dcfb4 0xcd47fd0e 0x2dafb216 0x27c89cd6 0xcd3c9aa0 0x79fc89c7 0x10aef18d 0x16218765 0x68f76705 0x04d6ee22
0xcf1a7584 0x048927ec 0x54051fda 0xc244ff28 0x901d2f40 0x7974b81c 0x378dcfb4 0xcd47fd0e 0x2dafb216 0x27c89cd6 0xcd3c9aa0 0x79fc89c7 0x10aef18d 0x16218765 0x68f76705 0x04d6ee22 0x03a14032 0x66b15927 0x9d6b6b42 0xb84c4109 0xa7143ae0 0xa09b33dd 0xa5daaf88 0x2fd91a73 0xc90c6b18 0x5a202413 0xc20e01b6 0x72cd6b74 0xba35d777 0xb360f1bf 0x8178315b 0x2cd11b1a
0x03a14032 0x66b15927 0x9d6b6b42 0xb84c4109 0xa7143ae0 0xa09b33dd 0xa5daaf88 0x2fd91a73 0xc90c6b18 0x5a202413 0xc20e01b6 0x72cd6b74 0xba35d777 0xb360f1bf 0x8178315b 0x2cd11b1a 0x9a2d3589 0x0b23fc4e 0x40af3b6b 0xceea8144 0x0a1bffc6 0x5e5993f7 0x9904c2e7 0x0d334718 0xe46c6354 0xc9503229 0x04fef5aa 0xf8933f72 0x2687d476 0x54e65231 0x3594ffc5 0x2b3bb2ca
0x9a2d3589 0x0b23fc4e 0x40af3b6b 0xceea8144 0x0a1bffc6 0x5e5993f7 0x9904c2e7 0x0d334718 0xe46c6354 0xc9503229 0x04fef5aa 0xf8933f72 0x2687d476 0x54e65231 0x3594ffc5 0x2b3bb2ca 0xc53318c5 0xca325d96 0x7e7d11cb 0x3404e2ca 0x26d7cf73 0x6088d379 0xc0f0e9bd 0xe310cdb9 0xae2ca8db 0x42f67c72 0x71669aca 0x975c171d 0x9e5ec228 0x7d85a9f3 0x201d0756 0x63fa6953
0xc53318c5 0xca325d96 0x7e7d11cb 0x3404e2ca 0x26d7cf73 0x6088d379 0xc0f0e9bd 0xe310cdb9 0xae2ca8db 0x42f67c72 0x71669aca 0x975c171d 0x9e5ec228 0x7d85a9f3 0x201d0756 0x63fa6953 0x04a3131a 0x66176309 0x0415bab1 0x61b880a2 0x36cc86c7 0xbf8a4465 0xf77dd720 0xfc0bdc90 0x07d13aca 0xeb0be9af 0x61599491 0x918512dc 0x33b6686d 0x795cc671 0xc0049972 0xa0a81bde
0x04a3131a 0x66176309 0x0415bab1 0x61b880a2 0x36cc86c7 0xbf8a4465 0xf77dd720 0xfc0bdc90 0x07d13aca 0xeb0be9af 0x61599491 0x918512dc 0x33b6686d 0x795cc671 0xc0049972 0xa0a81bde 0x9b70f51f 0x7ea8ac11 0x21e54da9 0xca393b2f 0x93b08686 0x6a4c50ae 0x19212a5a 0x9b032958 0xd839165e 0x4c06e28a 0xd3fde99e 0x26acc13d 0xa609f555 0x2c246549 0x95151853 0x2c847a0d
0x9b70f51f 0x7ea8ac11 0x21e54da9 0xca393b2f 0x93b08686 0x6a4c50ae 0x19212a5a 0x9b032958 0xd839165e 0x4c06e28a 0xd3fde99e 0x26acc13d 0xa609f555 0x2c246549 0x95151853 0x2c847a0d 0xca5c85dd 0x93a4f90e 0xd9f0df58 0x26dd82dd 0x982563f8 0x712aa9ff 0x279a61e8 0x970f72bd 0x1c25931a 0x5180bb10 0x779c27e7 0x54077e08 0xa9b751fb 0x382f3ce2 0x8db1757d 0xcc38080b
0xca5c85dd 0x93a4f90e 0xd9f0df58 0x26dd82dd 0x982563f8 0x712aa9ff 0x279a61e8 0x970f72bd 0x1c25931a 0x5180bb10 0x779c27e7 0x54077e08 0xa9b751fb 0x382f3ce2 0x8db1757d 0xcc38080b 0xb6b87de6 0x9a016148 0x93859815 0x4915e6cc 0xdc33c122 0x98e18fa3 0x5ffbe8fc 0xf7154b8b 0x28c1fcb3 0xc4b38f9d 0x83e2f5d7 0x7d24b98b 0x21078b22 0xb193e7a3 0xb2f49389 0x6cde6026
0xb6b87de6 0x9a016148 0x93859815 0x4915e6cc 0xdc33c122 0x98e18fa3 0x5ffbe8fc 0xf7154b8b 0x28c1fcb3 0xc4b38f9d 0x83e2f5d7 0x7d24b98b 0x21078b22 0xb193e7a3 0xb2f49389 0x6cde6026 0x837778ab 0xe238d763 0xa67ae21e 0x5950bb2f 0xc4f2d0c7 0xfc62bb2f 0x8fa018fc 0x3f5ec7b7 0x335271c2 0xf29489f3 0xeabda8fc 0x82e46ebd 0xd19c12b4 0xb04e16de 0x9e83d0cb 0x4e3c50a2
*/
