// Digital circuit main.dig as structural Verilog
module main (
  input  [63:0] k1,
  input  [63:0] k2,
  input  [63:0] k3,
  input  [63:0] k4,
  input  [63:0] k5,
  input  [63:0] k6,
  input  [63:0] k7,
  input  [63:0] k0,
  input  [63:0] n0,
  input  [63:0] n1,
  input  [63:0] n2
);

  wire block_function_1_p12, block_function_1_p13, block_function_1_p14, block_function_1_p15,
       block_function_1_p16, block_function_1_p17, block_function_1_p18, block_function_1_p19,
       block_function_1_p20, block_function_1_p21, block_function_1_p22, block_function_1_p23,
       block_function_1_p24, block_function_1_p25, block_function_1_p26, block_function_1_p27;

  // block_function block_function_1: pin names not known; wires that end beside it: k0, k1, k2, k3, k4, k5, k6, k7, n0, n1, n2, block_function_1_p12, block_function_1_p13, block_function_1_p14, block_function_1_p15, block_function_1_p16, block_function_1_p17, block_function_1_p18, block_function_1_p19, block_function_1_p20, block_function_1_p21, block_function_1_p22, block_function_1_p23, block_function_1_p24, block_function_1_p25, block_function_1_p26, block_function_1_p27, block_function_1_p27, block_function_1_p26, block_function_1_p25, block_function_1_p24, block_function_1_p23, block_function_1_p22, block_function_1_p21, block_function_1_p20, block_function_1_p19, block_function_1_p18, block_function_1_p17, block_function_1_p16, block_function_1_p15, block_function_1_p14, block_function_1_p13, block_function_1_p12

  // Notes on the sheet:
  //   Encryption Algorithm
  //   This counter is the i of the
  //   loop that iter throw text.
  //   counter>>8+text\_ptr is the start
  //   address of the data that is going 
  //   to be read
  //   key stream
endmodule
