// Digital circuit state_quarter_round.dig as structural Verilog
module state_quarter_round (
  input  [31:0] i0,
  input  [31:0] i1,
  input  [31:0] i2,
  input  [31:0] i3,
  input  [31:0] i4,
  input  [31:0] i5,
  input  [31:0] i6,
  input  [31:0] i7,
  input  [31:0] i8,
  input  [31:0] i9,
  input  [31:0] i10,
  input  [31:0] i11,
  input  [31:0] i12,
  input  [31:0] i13,
  input  [31:0] i14,
  input  [31:0] i15,
  input  [3:0] x,
  input  [3:0] y,
  input  [3:0] z,
  input  [3:0] w,
  output [31:0] o0,
  output [31:0] o1,
  output [31:0] o2,
  output [31:0] o3,
  output [31:0] o4,
  output [31:0] o5,
  output [31:0] o6,
  output [31:0] o7,
  output [31:0] o8,
  output [31:0] o9,
  output [31:0] o10,
  output [31:0] o11,
  output [31:0] o12,
  output [31:0] o13,
  output [31:0] o14,
  output [31:0] o15
);

  wire decoder_1_out_0, decoder_1_out_1, decoder_1_out_2, decoder_1_out_3, decoder_1_out_4, decoder_1_out_5,
       decoder_1_out_6, decoder_1_out_7, decoder_1_out_8, decoder_1_out_9, decoder_1_out_10,
       decoder_1_out_11, decoder_1_out_12, decoder_1_out_13, decoder_1_out_14, decoder_1_out_15,
       decoder_2_out_0, decoder_2_out_1, decoder_2_out_2, decoder_2_out_3, decoder_2_out_4, decoder_2_out_5,
       decoder_2_out_6, decoder_2_out_7, decoder_2_out_8, decoder_2_out_9, decoder_2_out_10,
       decoder_2_out_11, decoder_2_out_12, decoder_2_out_13, decoder_2_out_14, decoder_2_out_15,
       decoder_3_out_0, decoder_3_out_1, decoder_3_out_2, decoder_3_out_3, decoder_3_out_4, decoder_3_out_5,
       decoder_3_out_6, decoder_3_out_7, decoder_3_out_8, decoder_3_out_9, decoder_3_out_10,
       decoder_3_out_11, decoder_3_out_12, decoder_3_out_13, decoder_3_out_14, decoder_3_out_15,
       decoder_4_out_0, decoder_4_out_1, decoder_4_out_2, decoder_4_out_3, decoder_4_out_4, decoder_4_out_5,
       decoder_4_out_6, decoder_4_out_7, decoder_4_out_8, decoder_4_out_9, decoder_4_out_10,
       decoder_4_out_11, decoder_4_out_12, decoder_4_out_13, decoder_4_out_14, decoder_4_out_15;
  wire [31:0] A, B, C, D, multiplexer_1_out, multiplexer_2_out, multiplexer_3_out, multiplexer_4_out,
       multiplexer_5_out, multiplexer_6_out, multiplexer_7_out, multiplexer_8_out, multiplexer_9_out,
       multiplexer_10_out, multiplexer_11_out, multiplexer_12_out, multiplexer_13_out, multiplexer_14_out,
       multiplexer_15_out, multiplexer_16_out, multiplexer_17_out, multiplexer_18_out, multiplexer_19_out,
       multiplexer_20_out, multiplexer_21_out, multiplexer_22_out, multiplexer_23_out, multiplexer_24_out,
       multiplexer_25_out, multiplexer_26_out, multiplexer_27_out, multiplexer_28_out, multiplexer_29_out,
       multiplexer_30_out, multiplexer_31_out, multiplexer_32_out, multiplexer_33_out, multiplexer_34_out,
       multiplexer_35_out, multiplexer_36_out, multiplexer_37_out, multiplexer_38_out, multiplexer_39_out,
       multiplexer_40_out, multiplexer_41_out, multiplexer_42_out, multiplexer_43_out, multiplexer_44_out,
       multiplexer_45_out, multiplexer_46_out, multiplexer_47_out, multiplexer_48_out, multiplexer_49_out,
       multiplexer_50_out, multiplexer_51_out, multiplexer_52_out;

  Multiplexer #(.Selector_Bits(4), .Bits(32)) multiplexer_1 (
    .sel(x), .in_0(i0), .in_1(i1), .in_2(i2), .in_3(i3), .in_4(i4), .in_5(i5), .in_6(i6), .in_7(i7),
    .in_8(i8), .in_9(i9), .in_10(i10), .in_11(i11), .in_12(i12), .in_13(i13), .in_14(i14), .in_15(i15),
    .out(multiplexer_1_out));
  Multiplexer #(.Bits(32)) multiplexer_2 (.sel(decoder_1_out_0), .in_0(i0), .in_1(A), .out(multiplexer_2_out));
  Multiplexer #(.Bits(32)) multiplexer_3 (.sel(decoder_1_out_1), .in_0(i1), .in_1(A), .out(multiplexer_3_out));
  Multiplexer #(.Bits(32)) multiplexer_4 (.sel(decoder_1_out_2), .in_0(i2), .in_1(A), .out(multiplexer_4_out));
  Multiplexer #(.Bits(32)) multiplexer_5 (.sel(decoder_1_out_3), .in_0(i3), .in_1(A), .out(multiplexer_5_out));
  Multiplexer #(.Bits(32)) multiplexer_6 (.sel(decoder_1_out_4), .in_0(i4), .in_1(A), .out(multiplexer_6_out));
  Multiplexer #(.Bits(32)) multiplexer_7 (.sel(decoder_1_out_5), .in_0(i5), .in_1(A), .out(multiplexer_7_out));
  Multiplexer #(.Bits(32)) multiplexer_8 (.sel(decoder_1_out_6), .in_0(i6), .in_1(A), .out(multiplexer_8_out));
  Multiplexer #(.Bits(32)) multiplexer_9 (.sel(decoder_1_out_7), .in_0(i7), .in_1(A), .out(multiplexer_9_out));
  Multiplexer #(.Bits(32)) multiplexer_10 (.sel(decoder_1_out_8), .in_0(i8), .in_1(A), .out(multiplexer_10_out));
  Multiplexer #(.Bits(32)) multiplexer_11 (.sel(decoder_1_out_9), .in_0(i9), .in_1(A), .out(multiplexer_11_out));
  Multiplexer #(.Bits(32)) multiplexer_12 (.sel(decoder_1_out_10), .in_0(i10), .in_1(A), .out(multiplexer_12_out));
  Multiplexer #(.Bits(32)) multiplexer_13 (.sel(decoder_1_out_11), .in_0(i11), .in_1(A), .out(multiplexer_13_out));
  Multiplexer #(.Bits(32)) multiplexer_14 (.sel(decoder_1_out_12), .in_0(i12), .in_1(A), .out(multiplexer_14_out));
  Multiplexer #(.Bits(32)) multiplexer_15 (.sel(decoder_1_out_13), .in_0(i13), .in_1(A), .out(multiplexer_15_out));
  Multiplexer #(.Bits(32)) multiplexer_16 (.sel(decoder_1_out_14), .in_0(i14), .in_1(A), .out(multiplexer_16_out));
  Multiplexer #(.Bits(32)) multiplexer_17 (.sel(decoder_1_out_15), .in_0(i15), .in_1(A), .out(multiplexer_17_out));
  Multiplexer #(.Selector_Bits(4), .Bits(32)) multiplexer_18 (
    .sel(y), .in_0(i0), .in_1(i1), .in_2(i2), .in_3(i3), .in_4(i4), .in_5(i5), .in_6(i6), .in_7(i7),
    .in_8(i8), .in_9(i9), .in_10(i10), .in_11(i11), .in_12(i12), .in_13(i13), .in_14(i14), .in_15(i15),
    .out(multiplexer_18_out));
  Decoder #(.Selector_Bits(4)) decoder_1 (
    .sel(x), .out_0(decoder_1_out_0), .out_1(decoder_1_out_1), .out_2(decoder_1_out_2),
    .out_3(decoder_1_out_3), .out_4(decoder_1_out_4), .out_5(decoder_1_out_5), .out_6(decoder_1_out_6),
    .out_7(decoder_1_out_7), .out_8(decoder_1_out_8), .out_9(decoder_1_out_9), .out_10(decoder_1_out_10),
    .out_11(decoder_1_out_11), .out_12(decoder_1_out_12), .out_13(decoder_1_out_13),
    .out_14(decoder_1_out_14), .out_15(decoder_1_out_15));
  Multiplexer #(.Selector_Bits(4), .Bits(32)) multiplexer_19 (
    .sel(z), .in_0(i0), .in_1(i1), .in_2(i2), .in_3(i3), .in_4(i4), .in_5(i5), .in_6(i6), .in_7(i7),
    .in_8(i8), .in_9(i9), .in_10(i10), .in_11(i11), .in_12(i12), .in_13(i13), .in_14(i14), .in_15(i15),
    .out(multiplexer_19_out));
  Multiplexer #(.Bits(32)) multiplexer_20 (
    .sel(decoder_2_out_0), .in_0(multiplexer_2_out), .in_1(B), .out(multiplexer_20_out));
  Multiplexer #(.Bits(32)) multiplexer_21 (
    .sel(decoder_2_out_1), .in_0(multiplexer_3_out), .in_1(B), .out(multiplexer_21_out));
  Multiplexer #(.Bits(32)) multiplexer_22 (
    .sel(decoder_2_out_2), .in_0(multiplexer_4_out), .in_1(B), .out(multiplexer_22_out));
  Multiplexer #(.Bits(32)) multiplexer_23 (
    .sel(decoder_2_out_3), .in_0(multiplexer_5_out), .in_1(B), .out(multiplexer_23_out));
  Multiplexer #(.Bits(32)) multiplexer_24 (
    .sel(decoder_2_out_4), .in_0(multiplexer_6_out), .in_1(B), .out(multiplexer_24_out));
  Multiplexer #(.Bits(32)) multiplexer_25 (
    .sel(decoder_2_out_5), .in_0(multiplexer_7_out), .in_1(B), .out(multiplexer_25_out));
  Multiplexer #(.Bits(32)) multiplexer_26 (
    .sel(decoder_2_out_6), .in_0(multiplexer_8_out), .in_1(B), .out(multiplexer_26_out));
  Multiplexer #(.Bits(32)) multiplexer_27 (
    .sel(decoder_2_out_7), .in_0(multiplexer_9_out), .in_1(B), .out(multiplexer_27_out));
  Multiplexer #(.Bits(32)) multiplexer_28 (
    .sel(decoder_2_out_8), .in_0(multiplexer_10_out), .in_1(B), .out(multiplexer_28_out));
  Multiplexer #(.Bits(32)) multiplexer_29 (
    .sel(decoder_2_out_9), .in_0(multiplexer_11_out), .in_1(B), .out(multiplexer_29_out));
  Multiplexer #(.Bits(32)) multiplexer_30 (
    .sel(decoder_2_out_10), .in_0(multiplexer_12_out), .in_1(B), .out(multiplexer_30_out));
  Multiplexer #(.Bits(32)) multiplexer_31 (
    .sel(decoder_2_out_11), .in_0(multiplexer_13_out), .in_1(B), .out(multiplexer_31_out));
  Multiplexer #(.Bits(32)) multiplexer_32 (
    .sel(decoder_2_out_12), .in_0(multiplexer_14_out), .in_1(B), .out(multiplexer_32_out));
  Multiplexer #(.Bits(32)) multiplexer_33 (
    .sel(decoder_2_out_13), .in_0(multiplexer_15_out), .in_1(B), .out(multiplexer_33_out));
  Multiplexer #(.Bits(32)) multiplexer_34 (
    .sel(decoder_2_out_14), .in_0(multiplexer_16_out), .in_1(B), .out(multiplexer_34_out));
  Multiplexer #(.Bits(32)) multiplexer_35 (
    .sel(decoder_2_out_15), .in_0(multiplexer_17_out), .in_1(B), .out(multiplexer_35_out));
  Decoder #(.Selector_Bits(4)) decoder_2 (
    .sel(y), .out_0(decoder_2_out_0), .out_1(decoder_2_out_1), .out_2(decoder_2_out_2),
    .out_3(decoder_2_out_3), .out_4(decoder_2_out_4), .out_5(decoder_2_out_5), .out_6(decoder_2_out_6),
    .out_7(decoder_2_out_7), .out_8(decoder_2_out_8), .out_9(decoder_2_out_9), .out_10(decoder_2_out_10),
    .out_11(decoder_2_out_11), .out_12(decoder_2_out_12), .out_13(decoder_2_out_13),
    .out_14(decoder_2_out_14), .out_15(decoder_2_out_15));
  Multiplexer #(.Bits(32)) multiplexer_36 (
    .sel(decoder_3_out_0), .in_0(multiplexer_20_out), .in_1(C), .out(multiplexer_36_out));
  Multiplexer #(.Bits(32)) multiplexer_37 (
    .sel(decoder_3_out_1), .in_0(multiplexer_21_out), .in_1(C), .out(multiplexer_37_out));
  Multiplexer #(.Bits(32)) multiplexer_38 (
    .sel(decoder_3_out_2), .in_0(multiplexer_22_out), .in_1(C), .out(multiplexer_38_out));
  Multiplexer #(.Bits(32)) multiplexer_39 (
    .sel(decoder_3_out_3), .in_0(multiplexer_23_out), .in_1(C), .out(multiplexer_39_out));
  Multiplexer #(.Bits(32)) multiplexer_40 (
    .sel(decoder_3_out_4), .in_0(multiplexer_24_out), .in_1(C), .out(multiplexer_40_out));
  Multiplexer #(.Bits(32)) multiplexer_41 (
    .sel(decoder_3_out_5), .in_0(multiplexer_25_out), .in_1(C), .out(multiplexer_41_out));
  Multiplexer #(.Bits(32)) multiplexer_42 (
    .sel(decoder_3_out_6), .in_0(multiplexer_26_out), .in_1(C), .out(multiplexer_42_out));
  Multiplexer #(.Bits(32)) multiplexer_43 (
    .sel(decoder_3_out_7), .in_0(multiplexer_27_out), .in_1(C), .out(multiplexer_43_out));
  Multiplexer #(.Bits(32)) multiplexer_44 (
    .sel(decoder_3_out_8), .in_0(multiplexer_28_out), .in_1(C), .out(multiplexer_44_out));
  Multiplexer #(.Bits(32)) multiplexer_45 (
    .sel(decoder_3_out_9), .in_0(multiplexer_29_out), .in_1(C), .out(multiplexer_45_out));
  Multiplexer #(.Bits(32)) multiplexer_46 (
    .sel(decoder_3_out_10), .in_0(multiplexer_30_out), .in_1(C), .out(multiplexer_46_out));
  Multiplexer #(.Bits(32)) multiplexer_47 (
    .sel(decoder_3_out_11), .in_0(multiplexer_31_out), .in_1(C), .out(multiplexer_47_out));
  Multiplexer #(.Bits(32)) multiplexer_48 (
    .sel(decoder_3_out_12), .in_0(multiplexer_32_out), .in_1(C), .out(multiplexer_48_out));
  Multiplexer #(.Bits(32)) multiplexer_49 (
    .sel(decoder_3_out_13), .in_0(multiplexer_33_out), .in_1(C), .out(multiplexer_49_out));
  Multiplexer #(.Bits(32)) multiplexer_50 (
    .sel(decoder_3_out_14), .in_0(multiplexer_34_out), .in_1(C), .out(multiplexer_50_out));
  Multiplexer #(.Bits(32)) multiplexer_51 (
    .sel(decoder_3_out_15), .in_0(multiplexer_35_out), .in_1(C), .out(multiplexer_51_out));
  Multiplexer #(.Selector_Bits(4), .Bits(32)) multiplexer_52 (
    .sel(w), .in_0(i0), .in_1(i1), .in_2(i2), .in_3(i3), .in_4(i4), .in_5(i5), .in_6(i6), .in_7(i7),
    .in_8(i8), .in_9(i9), .in_10(i10), .in_11(i11), .in_12(i12), .in_13(i13), .in_14(i14), .in_15(i15),
    .out(multiplexer_52_out));
  quarter_round quarter_round_1 (
    .a(multiplexer_1_out), .b(multiplexer_18_out), .c(multiplexer_19_out), .d(multiplexer_52_out), .A_2(A),
    .B_2(B), .C_2(C), .D_2(D));
  Decoder #(.Selector_Bits(4)) decoder_3 (
    .sel(z), .out_0(decoder_3_out_0), .out_1(decoder_3_out_1), .out_2(decoder_3_out_2),
    .out_3(decoder_3_out_3), .out_4(decoder_3_out_4), .out_5(decoder_3_out_5), .out_6(decoder_3_out_6),
    .out_7(decoder_3_out_7), .out_8(decoder_3_out_8), .out_9(decoder_3_out_9), .out_10(decoder_3_out_10),
    .out_11(decoder_3_out_11), .out_12(decoder_3_out_12), .out_13(decoder_3_out_13),
    .out_14(decoder_3_out_14), .out_15(decoder_3_out_15));
  Multiplexer #(.Bits(32)) multiplexer_53 (.sel(decoder_4_out_0), .in_0(multiplexer_36_out), .in_1(D), .out(o0));
  Multiplexer #(.Bits(32)) multiplexer_54 (.sel(decoder_4_out_1), .in_0(multiplexer_37_out), .in_1(D), .out(o1));
  Multiplexer #(.Bits(32)) multiplexer_55 (.sel(decoder_4_out_2), .in_0(multiplexer_38_out), .in_1(D), .out(o2));
  Multiplexer #(.Bits(32)) multiplexer_56 (.sel(decoder_4_out_3), .in_0(multiplexer_39_out), .in_1(D), .out(o3));
  Multiplexer #(.Bits(32)) multiplexer_57 (.sel(decoder_4_out_4), .in_0(multiplexer_40_out), .in_1(D), .out(o4));
  Multiplexer #(.Bits(32)) multiplexer_58 (.sel(decoder_4_out_5), .in_0(multiplexer_41_out), .in_1(D), .out(o5));
  Multiplexer #(.Bits(32)) multiplexer_59 (.sel(decoder_4_out_6), .in_0(multiplexer_42_out), .in_1(D), .out(o6));
  Multiplexer #(.Bits(32)) multiplexer_60 (.sel(decoder_4_out_7), .in_0(multiplexer_43_out), .in_1(D), .out(o7));
  Multiplexer #(.Bits(32)) multiplexer_61 (.sel(decoder_4_out_8), .in_0(multiplexer_44_out), .in_1(D), .out(o8));
  Multiplexer #(.Bits(32)) multiplexer_62 (.sel(decoder_4_out_9), .in_0(multiplexer_45_out), .in_1(D), .out(o9));
  Multiplexer #(.Bits(32)) multiplexer_63 (.sel(decoder_4_out_10), .in_0(multiplexer_46_out), .in_1(D), .out(o10));
  Multiplexer #(.Bits(32)) multiplexer_64 (.sel(decoder_4_out_11), .in_0(multiplexer_47_out), .in_1(D), .out(o11));
  Multiplexer #(.Bits(32)) multiplexer_65 (.sel(decoder_4_out_12), .in_0(multiplexer_48_out), .in_1(D), .out(o12));
  Multiplexer #(.Bits(32)) multiplexer_66 (.sel(decoder_4_out_13), .in_0(multiplexer_49_out), .in_1(D), .out(o13));
  Multiplexer #(.Bits(32)) multiplexer_67 (.sel(decoder_4_out_14), .in_0(multiplexer_50_out), .in_1(D), .out(o14));
  Multiplexer #(.Bits(32)) multiplexer_68 (.sel(decoder_4_out_15), .in_0(multiplexer_51_out), .in_1(D), .out(o15));
  Decoder #(.Selector_Bits(4)) decoder_4 (
    .sel(w), .out_0(decoder_4_out_0), .out_1(decoder_4_out_1), .out_2(decoder_4_out_2),
    .out_3(decoder_4_out_3), .out_4(decoder_4_out_4), .out_5(decoder_4_out_5), .out_6(decoder_4_out_6),
    .out_7(decoder_4_out_7), .out_8(decoder_4_out_8), .out_9(decoder_4_out_9), .out_10(decoder_4_out_10),
    .out_11(decoder_4_out_11), .out_12(decoder_4_out_12), .out_13(decoder_4_out_13),
    .out_14(decoder_4_out_14), .out_15(decoder_4_out_15));
endmodule

/* Test case:
i0 i1 i2 i3 i4 i5 i6 i7 i8 i9 i10 i11 i12 i13 i14 i15 x y z w o0 o1 o2 o3 o4 o5 o6 o7 o8 o9 o10 o11 o12 o13 o14 o15
0x879531e0 0xc5ecf37d 0x516461b1 0xc9a62f8a 0x44c20ef3 0x3390af7f 0xd9fc690b 0x2a5f714c 0x53372767 0xb00a5631 0x974c541a 0x359e9963 0x5c971061 0x3d631689 0x2098d9d6 0x91dbd320 2 7 8 13 0x879531e0 0xc5ecf37d 0xbdb886dc 0xc9a62f8a 0x44c20ef3 0x3390af7f 0xd9fc690b 0xcfacafd2 0xe46bea80 0xb00a5631 0x974c541a 0x359e9963 0x5c971061 0xccc07c79 0x2098d9d6 0x91dbd320
*/
